// Logisim project S-R Flip Flop.circ as structural Verilog
module S_R_Flip_Flop (
  input  S,
  input  CLK,
  input  R,
  output Q,
  output Q_prime
);

  wire nand_1_out, nand_2_out;

  nand nand_1 (nand_1_out, S, CLK);
  nand nand_2 (nand_2_out, CLK, R);
  nand nand_3 (Q, nand_1_out, Q_prime);
  nand nand_4 (Q_prime, Q, nand_2_out);
endmodule

module _16_bit_reg (
);

  S_R_Flip_Flop s_r_flip_flop_1 ();  // open: S, CLK, R, Q, Q_prime
  S_R_Flip_Flop s_r_flip_flop_2 ();  // open: S, CLK, R, Q, Q_prime
endmodule

module _1_bit_register (
  input  Clock,
  input  Data,
  input  Load,
  output Output
);

  wire and_1_out, and_2_out, not_1_out;

  not not_1 (not_1_out, Data);
  and and_1 (and_1_out, Data, Load);
  and and_2 (and_2_out, not_1_out, Load);
  S_R_Flip_Flop s_r_flip_flop_1 (.S(and_1_out), .CLK(Clock), .R(and_2_out), .Q(Output));  // open: Q_prime
endmodule
