// Logisim project Design.circ as structural Verilog
module S_R_Flip_Flop (
  input  S,
  input  Clock,
  input  R,
  output Q,
  output Q_prime
);

  wire nand_1_out, nand_2_out;

  nand nand_1 (nand_1_out, S, Clock);
  nand nand_2 (nand_2_out, Clock, R);
  nand nand_3 (Q, nand_1_out, Q_prime);
  nand nand_4 (Q_prime, Q, nand_2_out);
endmodule

module _1_bit_Register (
  input  Clock,
  input  D,
  input  Load,
  output Q
);

  wire and_1_out, and_2_out, not_1_out;

  not not_1 (not_1_out, D);
  and and_1 (and_1_out, D, Load);
  and and_2 (and_2_out, not_1_out, Load);
  S_R_Flip_Flop s_r_flip_flop_1 (.S(and_1_out), .Clock(Clock), .R(and_2_out), .Q(Q));  // open: Q_prime
endmodule

module _16_bit_Register (
  input  Clock,
  input  [15:0] in_2,
  input  Load,
  output [15:0] out_4
);

  _1_bit_Register u_1_bit_register_1 (.Clock(Clock), .D(in_2[0]), .Load(Load), .Q(out_4[0]));
  _1_bit_Register u_1_bit_register_2 (.Clock(Clock), .D(in_2[1]), .Load(Load), .Q(out_4[1]));
  _1_bit_Register u_1_bit_register_3 (.Clock(Clock), .D(in_2[2]), .Load(Load), .Q(out_4[2]));
  _1_bit_Register u_1_bit_register_4 (.Clock(Clock), .D(in_2[3]), .Load(Load), .Q(out_4[3]));
  _1_bit_Register u_1_bit_register_5 (.Clock(Clock), .D(in_2[4]), .Load(Load), .Q(out_4[4]));
  _1_bit_Register u_1_bit_register_6 (.Clock(Clock), .D(in_2[5]), .Load(Load), .Q(out_4[5]));
  _1_bit_Register u_1_bit_register_7 (.Clock(Clock), .D(in_2[6]), .Load(Load), .Q(out_4[6]));
  _1_bit_Register u_1_bit_register_8 (.Clock(Clock), .D(in_2[7]), .Load(Load), .Q(out_4[7]));
  _1_bit_Register u_1_bit_register_9 (.Clock(Clock), .D(in_2[8]), .Load(Load), .Q(out_4[8]));
  _1_bit_Register u_1_bit_register_10 (.Clock(Clock), .D(in_2[9]), .Load(Load), .Q(out_4[9]));
  _1_bit_Register u_1_bit_register_11 (.Clock(Clock), .D(in_2[10]), .Load(Load), .Q(out_4[10]));
  _1_bit_Register u_1_bit_register_12 (.Clock(Clock), .D(in_2[11]), .Load(Load), .Q(out_4[11]));
  _1_bit_Register u_1_bit_register_13 (.Clock(Clock), .D(in_2[12]), .Load(Load), .Q(out_4[12]));
  _1_bit_Register u_1_bit_register_14 (.Clock(Clock), .D(in_2[13]), .Load(Load), .Q(out_4[13]));
  _1_bit_Register u_1_bit_register_15 (.Clock(Clock), .D(in_2[14]), .Load(Load), .Q(out_4[14]));
  _1_bit_Register u_1_bit_register_16 (.Clock(Clock), .D(in_2[15]), .Load(Load), .Q(out_4[15]));
endmodule

module Register_Bank (
  input  in_1,
  input  [2:0] in_2,
  input  RegLoad,
  input  [15:0] in_4,
  output [15:0] out_5,
  output [15:0] out_6,
  output [15:0] out_7,
  output [15:0] out_8,
  output [15:0] out_9,
  output [15:0] out_10,
  output [15:0] out_11,
  output [15:0] out_12
);

  wire and_1_out, and_2_out, and_3_out, and_4_out, and_5_out, and_6_out, and_7_out, and_8_out,
       decoder_1_out0, decoder_1_out1, decoder_1_out2, decoder_1_out3, decoder_1_out4, decoder_1_out5,
       decoder_1_out6, decoder_1_out7;

  Decoder #(.select(3), .enable("false")) decoder_1 (
    .out0(decoder_1_out0), .out1(decoder_1_out1), .out2(decoder_1_out2), .out3(decoder_1_out3),
    .out4(decoder_1_out4), .out5(decoder_1_out5), .out6(decoder_1_out6), .out7(decoder_1_out7), .sel(in_2));
  and and_1 (and_1_out, decoder_1_out0, RegLoad);
  and and_2 (and_2_out, decoder_1_out1, RegLoad);
  and and_3 (and_3_out, decoder_1_out2, RegLoad);
  and and_4 (and_4_out, decoder_1_out3, RegLoad);
  and and_5 (and_5_out, decoder_1_out4, RegLoad);
  and and_6 (and_6_out, decoder_1_out5, RegLoad);
  and and_7 (and_7_out, decoder_1_out6, RegLoad);
  and and_8 (and_8_out, decoder_1_out7, RegLoad);
  _16_bit_Register u_16_bit_register_1 (.Clock(in_1), .in_2(in_4), .Load(and_1_out), .out_4(out_5));
  _16_bit_Register u_16_bit_register_2 (.Clock(in_1), .in_2(in_4), .Load(and_2_out), .out_4(out_6));
  _16_bit_Register u_16_bit_register_3 (.Clock(in_1), .in_2(in_4), .Load(and_3_out), .out_4(out_7));
  _16_bit_Register u_16_bit_register_4 (.Clock(in_1), .in_2(in_4), .Load(and_4_out), .out_4(out_8));
  _16_bit_Register u_16_bit_register_5 (.Clock(in_1), .in_2(in_4), .Load(and_5_out), .out_4(out_9));
  _16_bit_Register u_16_bit_register_6 (.Clock(in_1), .in_2(in_4), .Load(and_6_out), .out_4(out_10));
  _16_bit_Register u_16_bit_register_7 (.Clock(in_1), .in_2(in_4), .Load(and_7_out), .out_4(out_11));
  _16_bit_Register u_16_bit_register_8 (.Clock(in_1), .in_2(in_4), .Load(and_8_out), .out_4(out_12));
endmodule

module ALU (
  input  [15:0] In1,
  input  [15:0] In2,
  input  [2:0] in_3,
  input  in_4,
  input  [2:0] in_5,
  output [15:0] out_6
);

  wire adder_2_cout;
  wire [15:0] adder_1_out, adder_2_out, and_1_out, multiplexer_2_out, nor_1_out, not_1_out, or_1_out,
       subtractor_1_out, subtractor_2_out;

  Adder #(.width(16)) adder_1 (.a(In2), .b(In1), .out(adder_1_out));  // open: cin, cout
  Subtractor #(.width(16)) subtractor_1 (.a(In2), .b(In1), .out(subtractor_1_out));  // open: bin, bout
  assign and_1_out = In1 & In2;  // AND_Gate and_1, 16 bits wide
  assign or_1_out = In1 | In2;  // OR_Gate or_1, 16 bits wide
  assign nor_1_out = ~(In1 | In2);  // NOR_Gate nor_1, 16 bits wide
  Multiplexer #(.select(3), .width(16), .enable("false")) multiplexer_1 (
    .in0(adder_1_out), .in1(subtractor_1_out), .in2(and_1_out), .in3(or_1_out), .in4(nor_1_out),
    .in7(multiplexer_2_out), .out(out_6), .sel(in_5));  // open: in5, in6
  assign not_1_out = ~In1;  // NOT_Gate not_1, 16 bits wide
  Adder #(.width(16)) adder_2 (.a(In1), .b(16'h1), .out(adder_2_out), .cout(adder_2_cout));  // open: cin
  Multiplexer #(.select(3), .width(16)) multiplexer_2 (
    .in0(In1), .in1(not_1_out), .in2(adder_2_out), .in3(subtractor_2_out), .out(multiplexer_2_out),
    .sel(in_3), .en(in_4));  // open: in4, in5, in6, in7
  Subtractor #(.width(16)) subtractor_2 (.a(In1), .b(16'h1), .out(subtractor_2_out));  // open: bin, bout
endmodule
